// Logisim project Mux.circ as structural Verilog: 1 circuit, main circuit main
module main (
  input  A,
  input  B,
  input  SEL,
  output OUT
);

  wire and_1_out, and_2_out, and_3_out, and_4_out, and_5_out, nand_1_out, nand_2_out, nand_3_out, nand_4_out,
       not_1_out, not_2_out, not_3_out;

  not not_1 (not_1_out, A);
  not not_2 (not_2_out, B);
  and and_1 (and_1_out, not_1_out, B);
  and and_2 (and_2_out, A, not_2_out);
  and and_3 (and_3_out, A, B);
  not not_3 (not_3_out, SEL);
  nand nand_1 (nand_1_out, and_1_out, SEL);
  nand nand_2 (nand_2_out, and_2_out, not_3_out);
  nand nand_3 (nand_3_out, and_3_out, not_3_out);
  nand nand_4 (nand_4_out, and_3_out, SEL);
  and and_4 (and_4_out, nand_1_out, nand_2_out);
  and and_5 (and_5_out, nand_3_out, nand_4_out);
  nand nand_5 (OUT, and_4_out, and_5_out);
endmodule
