// Logisim project Or.circ as structural Verilog: 1 circuit, main circuit main
module main (
  input  A,
  input  B,
  output OUT
);

  wire not_1_out, not_2_out;

  not not_1 (not_1_out, A);
  not not_2 (not_2_out, B);
  nand nand_1 (OUT, not_1_out, not_2_out);
endmodule
