// Logisim project Dmux.circ as structural Verilog: 1 circuit, main circuit main
module main (
  input  IN,
  input  SEL,
  output A,
  output B
);

  wire not_1_out;

  not not_1 (not_1_out, SEL);
  and and_1 (A, IN, not_1_out);
  and and_2 (B, IN, SEL);
endmodule
