// Logisim project Mux16.circ as structural Verilog: 1 circuit, main circuit main
module main (
  input  Sel,
  input  in_2,
  input  in_3,
  input  in_4,
  input  in_5,
  input  in_6,
  input  in_7,
  input  in_8,
  input  in_9,
  input  in_10,
  input  in_11,
  input  in_12,
  input  in_13,
  input  in_14,
  input  in_15,
  input  in_16,
  input  in_17,
  input  in_18,
  input  in_19,
  input  in_20,
  input  in_21,
  input  in_22,
  input  in_23,
  input  in_24,
  input  in_25,
  input  in_26,
  input  in_27,
  input  in_28,
  input  in_29,
  input  in_30,
  input  in_31,
  input  in_32,
  input  in_33,
  output out_34,
  output out_35,
  output out_36,
  output out_37,
  output out_38,
  output out_39,
  output out_40,
  output out_41,
  output out_42,
  output out_43,
  output out_44,
  output out_45,
  output out_46,
  output out_47,
  output out_48,
  output out_49
);

  Multiplexer #(.enable("false")) multiplexer_1 (.in0(in_2), .in1(in_3), .out(out_34), .sel(Sel));
  Multiplexer #(.enable("false")) multiplexer_2 (.in0(in_4), .in1(in_5), .out(out_35), .sel(Sel));
  Multiplexer #(.enable("false")) multiplexer_3 (.in0(in_6), .in1(in_7), .out(out_36), .sel(Sel));
  Multiplexer #(.enable("false")) multiplexer_4 (.in0(in_8), .in1(in_9), .out(out_37), .sel(Sel));
  Multiplexer #(.enable("false")) multiplexer_5 (.in0(in_10), .in1(in_11), .out(out_38), .sel(Sel));
  Multiplexer #(.enable("false")) multiplexer_6 (.in0(in_12), .in1(in_13), .out(out_39), .sel(Sel));
  Multiplexer #(.enable("false")) multiplexer_7 (.in0(in_14), .in1(in_15), .out(out_40), .sel(Sel));
  Multiplexer #(.enable("false")) multiplexer_8 (.in0(in_16), .in1(in_17), .out(out_41), .sel(Sel));
  Multiplexer #(.enable("false")) multiplexer_9 (.in0(in_18), .in1(in_19), .out(out_42), .sel(Sel));
  Multiplexer #(.enable("false")) multiplexer_10 (.in0(in_20), .in1(in_21), .out(out_43), .sel(Sel));
  Multiplexer #(.enable("false")) multiplexer_11 (.in0(in_22), .in1(in_23), .out(out_44), .sel(Sel));
  Multiplexer #(.enable("false")) multiplexer_12 (.in0(in_24), .in1(in_25), .out(out_45), .sel(Sel));
  Multiplexer #(.enable("false")) multiplexer_13 (.in0(in_26), .in1(in_27), .out(out_46), .sel(Sel));
  Multiplexer #(.enable("false")) multiplexer_14 (.in0(in_28), .in1(in_29), .out(out_47), .sel(Sel));
  Multiplexer #(.enable("false")) multiplexer_15 (.in0(in_30), .in1(in_31), .out(out_48), .sel(Sel));
  Multiplexer #(.enable("false")) multiplexer_16 (.in0(in_32), .in1(in_33), .out(out_49), .sel(Sel));
endmodule
