// Logisim project Mux8Way16.circ as structural Verilog: 1 circuit, main circuit Mux8Way16
module Mux8Way16 (
  input  [15:0] A,
  input  [15:0] B,
  input  [15:0] C,
  input  [15:0] D,
  input  [15:0] E,
  input  [15:0] F,
  input  [15:0] G,
  input  [15:0] H,
  input  [2:0] Sel,
  output [15:0] Out
);

  wire [15:0] main_1_out_6, main_2_out_6;

  Mux4Way16_main main_1 (.in_1(A), .in_2(B), .in_3(C), .in_4(D), .in_5(Sel[1:0]), .out_6(main_1_out_6));
  Mux4Way16_main main_2 (.in_1(E), .in_2(F), .in_3(G), .in_4(H), .in_5(Sel[1:0]), .out_6(main_2_out_6));
  Multiplexer #(.width(16), .enable("false")) multiplexer_1 (
    .in0(main_1_out_6), .in1(main_2_out_6), .out(Out), .sel(Sel[2]));
endmodule
