// Logisim project ALU.circ as structural Verilog: 1 circuit, main circuit main
module main (
  input  [15:0] X,
  input  [15:0] Y,
  input  zx,
  input  nx,
  input  zy,
  input  ny,
  input  f,
  input  no,
  output [15:0] Out,
  output ng,
  output zr
);

  wire main_2_out_9, main_3_out_9;
  wire [15:0] and_1_out, main_1_out_3, multiplexer_1_out, multiplexer_2_out, multiplexer_3_out,
       multiplexer_4_out, multiplexer_5_out, not_1_out, not_2_out, not_3_out;

  assign not_1_out = ~multiplexer_1_out;  // NOT_Gate not_1, 16 bits wide
  Multiplexer #(.width(16), .enable("false")) multiplexer_1 (
    .in0(X), .in1({16{1'b0}}), .out(multiplexer_1_out), .sel(zx));
  Multiplexer #(.width(16), .enable("false")) multiplexer_2 (
    .in0(Y), .in1({16{1'b0}}), .out(multiplexer_2_out), .sel(zy));
  Multiplexer #(.width(16), .enable("false")) multiplexer_3 (
    .in0(not_1_out), .in1(multiplexer_1_out), .out(multiplexer_3_out), .sel(nx));
  assign not_2_out = ~multiplexer_2_out;  // NOT_Gate not_2, 16 bits wide
  Multiplexer #(.width(16), .enable("false")) multiplexer_4 (
    .in0(not_2_out), .in1(multiplexer_2_out), .out(multiplexer_4_out), .sel(ny));
  assign and_1_out = multiplexer_3_out & multiplexer_4_out;  // AND_Gate and_1, 16 bits wide
  assign not_3_out = ~multiplexer_5_out;  // NOT_Gate not_3, 16 bits wide
  Multiplexer #(.width(16), .enable("false")) multiplexer_5 (
    .in0(and_1_out), .in1(main_1_out_3), .out(multiplexer_5_out), .sel(f));
  Add16_main main_1 (.A(multiplexer_3_out), .B(multiplexer_4_out), .out_3(main_1_out_3));
  Multiplexer #(.width(16), .enable("false")) multiplexer_6 (
    .in0(not_3_out), .in1(multiplexer_5_out), .out({ng, Out[14:0]}), .sel(no));
  Or8Way_main main_2 (
    .in_1(Out[0]), .in_2(Out[1]), .in_3(Out[2]), .in_4(Out[3]), .in_5(Out[4]), .in_6(Out[5]), .in_7(Out[6]),
    .in_8(Out[7]), .out_9(main_2_out_9));
  Or8Way_main main_3 (
    .in_1(Out[8]), .in_2(Out[9]), .in_3(Out[10]), .in_4(Out[11]), .in_5(Out[12]), .in_6(Out[13]),
    .in_7(Out[14]), .in_8(ng), .out_9(main_3_out_9));
  or or_1 (zr, main_2_out_9, main_3_out_9);

  assign Out[15] = ng;
endmodule
