// Logisim project Add16.circ as structural Verilog: 1 circuit, main circuit main
module main (
  input  [15:0] A,
  input  [15:0] B,
  output [15:0] out_3
);

  wire main_1_carry, main_2_carry, main_3_carry, main_4_carry, main_5_carry, main_6_carry, main_7_carry,
       main_8_carry, main_9_carry, main_10_carry, main_11_carry, main_12_carry, main_13_carry, main_14_carry,
       main_15_carry;

  HalfAdder_main main_1 (.A(A[0]), .B(B[0]), .Sum(out_3[0]), .Carry(main_1_carry));
  FullAdder_main main_2 (.A(A[1]), .B(B[1]), .Sum(out_3[1]), .Carry(main_2_carry), .C(main_1_carry));
  FullAdder_main main_3 (.A(A[2]), .B(B[2]), .Sum(out_3[2]), .Carry(main_3_carry), .C(main_2_carry));
  FullAdder_main main_4 (.A(A[3]), .B(B[3]), .Sum(out_3[3]), .Carry(main_4_carry), .C(main_3_carry));
  FullAdder_main main_5 (.A(A[4]), .B(B[4]), .Sum(out_3[4]), .Carry(main_5_carry), .C(main_4_carry));
  FullAdder_main main_6 (.A(A[5]), .B(B[5]), .Sum(out_3[5]), .Carry(main_6_carry), .C(main_5_carry));
  FullAdder_main main_7 (.A(A[6]), .B(B[6]), .Sum(out_3[6]), .Carry(main_7_carry), .C(main_6_carry));
  FullAdder_main main_8 (.A(A[7]), .B(B[7]), .Sum(out_3[7]), .Carry(main_8_carry), .C(main_7_carry));
  FullAdder_main main_9 (.A(A[8]), .B(B[8]), .Sum(out_3[8]), .Carry(main_9_carry), .C(main_8_carry));
  FullAdder_main main_10 (.A(A[9]), .B(B[9]), .Sum(out_3[9]), .Carry(main_10_carry), .C(main_9_carry));
  FullAdder_main main_11 (.A(A[10]), .B(B[10]), .Sum(out_3[10]), .Carry(main_11_carry), .C(main_10_carry));
  FullAdder_main main_12 (.A(A[11]), .B(B[11]), .Sum(out_3[11]), .Carry(main_12_carry), .C(main_11_carry));
  FullAdder_main main_13 (.A(A[12]), .B(B[12]), .Sum(out_3[12]), .Carry(main_13_carry), .C(main_12_carry));
  FullAdder_main main_14 (.A(A[13]), .B(B[13]), .Sum(out_3[13]), .Carry(main_14_carry), .C(main_13_carry));
  FullAdder_main main_15 (.A(A[14]), .B(B[14]), .Sum(out_3[14]), .Carry(main_15_carry), .C(main_14_carry));
  FullAdder_main main_16 (.A(A[15]), .B(B[15]), .Sum(out_3[15]), .C(main_15_carry));  // open: Carry
endmodule
