// Logisim project FullAdder.circ as structural Verilog: 1 circuit, main circuit main
module main (
  input  A,
  input  B,
  input  C,
  output Sum,
  output Carry
);

  wire main_1_carry, main_1_sum, main_2_carry;

  HalfAdder_main main_1 (.A(A), .B(B), .Sum(main_1_sum), .Carry(main_1_carry));
  HalfAdder_main main_2 (.A(main_1_sum), .B(C), .Sum(Sum), .Carry(main_2_carry));
  or or_1 (Carry, main_2_carry, main_1_carry);
endmodule
