// Logisim project Inc16.circ as structural Verilog: 1 circuit, main circuit main
module main (
  input  [15:0] IN,
  output [15:0] OUT
);

  Add16_main main_1 (.A(IN), .B(16'h1), .out_3(OUT));
endmodule
