// Logisim project Bit.circ as structural Verilog: 1 circuit, main circuit Bit
module Bit (
  input  In,
  input  Load,
  output Out
);

  wire clock_1_out, multiplexer_1_out;

  Multiplexer #(.enable("false")) multiplexer_1 (.in0(Out), .in1(In), .out(multiplexer_1_out), .sel(Load));
  Clock clock_1 (.out(clock_1_out));
  D_Flip_Flop d_ff_1 (.clk(clock_1_out), .D(multiplexer_1_out), .Q(Out));  // open: Qn, preset, en, reset
endmodule
