// Logisim project PC.circ as structural Verilog: 1 circuit, main circuit PC
module PC (
  input  [15:0] Input,
  input  Inc,
  input  Load,
  input  Reset,
  output [15:0] Out
);

  wire [15:0] main_1_out_3, mux8way16_1_out;

  Register register_1 (.In(mux8way16_1_out), .Load(1'b1), .Out(Out));
  Add16_main main_1 (.A(Out), .B(16'h1), .out_3(main_1_out_3));
  Mux8Way16 mux8way16_1 (
    .A(Out), .B(main_1_out_3), .C(Input), .D(Input), .E({16{1'b0}}), .F({16{1'b0}}), .G({16{1'b0}}),
    .H({16{1'b0}}), .Sel({Reset, Load, Inc}), .Out(mux8way16_1_out));
endmodule
