// Logisim project RAM16.circ as structural Verilog: 1 circuit, main circuit RAM16
module RAM16 (
  input  [15:0] In,
  input  [5:0] Address,
  input  Load,
  output [15:0] Output
);

  wire main_1_p3, main_1_p4, main_1_p5, main_1_p6, main_1_p7, main_1_p8, main_1_p9, main_1_p10;
  wire [15:0] ram8_1_out, ram8_2_out, ram8_3_out, ram8_4_out, ram8_5_out, ram8_6_out, ram8_7_out, ram8_8_out;

  // DMux8Way_main main_1: pin names not known; wires that end beside it: Load, Address[5:3], main_1_p3, main_1_p4, main_1_p5, main_1_p6, main_1_p7, main_1_p8, main_1_p9, main_1_p10
  RAM8 ram8_1 (.In(In), .Load(main_1_p3), .Address(Address[2:0]), .Out(ram8_1_out));
  RAM8 ram8_2 (.In(In), .Load(main_1_p4), .Address(Address[2:0]), .Out(ram8_2_out));
  RAM8 ram8_3 (.In(In), .Load(main_1_p5), .Address(Address[2:0]), .Out(ram8_3_out));
  RAM8 ram8_4 (.In(In), .Load(main_1_p6), .Address(Address[2:0]), .Out(ram8_4_out));
  RAM8 ram8_5 (.In(In), .Load(main_1_p7), .Address(Address[2:0]), .Out(ram8_5_out));
  RAM8 ram8_6 (.In(In), .Load(main_1_p8), .Address(Address[2:0]), .Out(ram8_6_out));
  RAM8 ram8_7 (.In(In), .Load(main_1_p9), .Address(Address[2:0]), .Out(ram8_7_out));
  RAM8 ram8_8 (.In(In), .Load(main_1_p10), .Address(Address[2:0]), .Out(ram8_8_out));
  Mux8Way16 mux8way16_1 (
    .A(ram8_1_out), .B(ram8_2_out), .C(ram8_3_out), .D(ram8_4_out), .E(ram8_5_out), .F(ram8_6_out),
    .G(ram8_7_out), .H(ram8_8_out), .Sel(Address[5:3]), .Out(Output));
endmodule
