// Logisim project RAM8.circ as structural Verilog: 1 circuit, main circuit RAM8
module RAM8 (
  input  [15:0] In,
  input  Load,
  input  [2:0] Address,
  output [15:0] Out
);

  wire main_1_p3, main_1_p4, main_1_p5, main_1_p6, main_1_p7, main_1_p8, main_1_p9, main_1_p10;
  wire [15:0] register_1_out, register_2_out, register_3_out, register_4_out, register_5_out, register_6_out,
       register_7_out, register_8_out;

  // DMux8Way_main main_1: pin names not known; wires that end beside it: Load, Address, main_1_p3, main_1_p4, main_1_p5, main_1_p6, main_1_p7, main_1_p8, main_1_p9, main_1_p10
  Register register_1 (.In(In), .Load(main_1_p3), .Out(register_1_out));
  Register register_2 (.In(In), .Load(main_1_p4), .Out(register_2_out));
  Register register_3 (.In(In), .Load(main_1_p5), .Out(register_3_out));
  Register register_4 (.In(In), .Load(main_1_p6), .Out(register_4_out));
  Register register_5 (.In(In), .Load(main_1_p7), .Out(register_5_out));
  Register register_6 (.In(In), .Load(main_1_p8), .Out(register_6_out));
  Register register_7 (.In(In), .Load(main_1_p9), .Out(register_7_out));
  Register register_8 (.In(In), .Load(main_1_p10), .Out(register_8_out));
  Mux8Way16 mux8way16_1 (
    .A(register_1_out), .B(register_2_out), .C(register_3_out), .D(register_4_out), .E(register_5_out),
    .F(register_6_out), .G(register_7_out), .H(register_8_out), .Sel(Address), .Out(Out));
endmodule
