// Logisim project Register.circ as structural Verilog: 1 circuit, main circuit Register
module Register (
  input  [15:0] In,
  input  Load,
  output [15:0] Out
);

  Bit bit_1 (.In(In[0]), .Load(Load), .Out(Out[0]));
  Bit bit_2 (.In(In[1]), .Load(Load), .Out(Out[1]));
  Bit bit_3 (.In(In[2]), .Load(Load), .Out(Out[2]));
  Bit bit_4 (.In(In[3]), .Load(Load), .Out(Out[3]));
  Bit bit_5 (.In(In[4]), .Load(Load), .Out(Out[4]));
  Bit bit_6 (.In(In[5]), .Load(Load), .Out(Out[5]));
  Bit bit_7 (.In(In[6]), .Load(Load), .Out(Out[6]));
  Bit bit_8 (.In(In[7]), .Load(Load), .Out(Out[7]));
  Bit bit_9 (.In(In[8]), .Load(Load), .Out(Out[8]));
  Bit bit_10 (.In(In[9]), .Load(Load), .Out(Out[9]));
  Bit bit_11 (.In(In[10]), .Load(Load), .Out(Out[10]));
  Bit bit_12 (.In(In[11]), .Load(Load), .Out(Out[11]));
  Bit bit_13 (.In(In[12]), .Load(Load), .Out(Out[12]));
  Bit bit_14 (.In(In[13]), .Load(Load), .Out(Out[13]));
  Bit bit_15 (.In(In[14]), .Load(Load), .Out(Out[14]));
  Bit bit_16 (.In(In[15]), .Load(Load), .Out(Out[15]));
endmodule
