// Logisim project CPU.circ as structural Verilog: 1 circuit, main circuit HackCPU
module HackCPU (
  input  [15:0] instruction,
  input  Reset,
  input  [15:0] inM,
  output writeM,
  output [15:0] outM,
  output [14:0] addressM,
  output [14:0] pc
);

  wire and_1_out, and_2_out, and_3_out, and_4_out, and_5_out, and_6_out, main_1_ng, main_1_zr, not_1_out,
       not_2_out, not_3_out, not_4_out, or_1_out, or_2_out;
  wire [15:0] D_Register_out, multiplexer_1_out, multiplexer_2_out;
  wire [15:15] A_Register_out, pc_1_out;

  Register D_Register (.In(outM), .Load(and_5_out), .Out(D_Register_out));
  Register A_Register (.In(multiplexer_2_out), .Load(or_1_out), .Out({A_Register_out[15], addressM}));
  Multiplexer #(.width(16), .enable("false")) multiplexer_1 (
    .in0({A_Register_out[15], addressM}), .in1(inM), .out(multiplexer_1_out), .sel(instruction[12]));
  PC pc_1 (
    .Input({A_Register_out[15], addressM}), .Load(and_6_out), .Inc(not_4_out), .Reset(Reset),
    .Out({pc_1_out[15], pc}));
  not not_1 (not_1_out, main_1_zr);
  not not_2 (not_2_out, main_1_ng);
  not not_3 (not_3_out, instruction[15]);
  or or_1 (or_1_out, instruction[5], not_3_out);
  ALU_main main_1 (
    .X(D_Register_out), .Y(multiplexer_1_out), .zx(instruction[11]), .nx(instruction[10]),
    .zy(instruction[9]), .ny(instruction[8]), .f(instruction[7]), .no(instruction[6]), .Out(outM),
    .ng(main_1_ng), .zr(main_1_zr));
  and and_1 (and_1_out, not_2_out, not_1_out, instruction[0]);
  and and_2 (and_2_out, not_2_out, main_1_zr, instruction[1]);
  and and_3 (and_3_out, main_1_ng, not_1_out, instruction[2]);
  and and_4 (and_4_out, instruction[0], instruction[1], instruction[2]);
  and and_5 (and_5_out, instruction[15], instruction[4]);
  or or_2 (or_2_out, and_1_out, and_2_out, and_3_out, and_4_out);
  Multiplexer #(.width(16), .enable("false")) multiplexer_2 (
    .in0(outM), .in1(instruction), .out(multiplexer_2_out), .sel(not_3_out));
  and and_6 (and_6_out, or_2_out, instruction[15]);
  not not_4 (not_4_out, and_6_out);
  and and_7 (writeM, instruction[15], instruction[3]);
endmodule
