// Logisim project HackComputer.circ as structural Verilog: 1 circuit, main circuit main
module main (
);

  wire button_1_out, hackcpu_1_writem;
  wire [14:0] hackcpu_1_addressm, hackcpu_1_pc;
  wire [15:0] hackcpu_1_outm, memory_1_out, rom_1_data;

  Button button_1 (.out(button_1_out));
  HackCPU hackcpu_1 (
    .instruction(rom_1_data), .Reset(button_1_out), .inM(memory_1_out), .writeM(hackcpu_1_writem),
    .outM(hackcpu_1_outm), .addressM(hackcpu_1_addressm), .pc(hackcpu_1_pc));
  Clock clock_1 ();  // open: out
  ROM #(.addrWidth(15), .dataWidth(16)) rom_1 (.addr(hackcpu_1_pc), .data(rom_1_data));  // open: sel
  Memory memory_1 (.Address(hackcpu_1_addressm), .Load(hackcpu_1_writem), .In(hackcpu_1_outm), .Out(memory_1_out));

  // Notes on the sheet:
  //   contents of rom_1 (hex, n*v repeats v):
  //   0 0 1 0 1110 1010 1000 1000 4*0 1111 1100 1 0 0 0 1 1
endmodule
