// Logisim project Memory.circ as structural Verilog: 1 circuit, main circuit Memory
module Memory (
  input  [14:0] Address,
  input  Load,
  input  [15:0] In,
  output [15:0] Out
);

  wire clock_1_out, demultiplexer_1_out0;

  Demultiplexer #(.enable("false")) demultiplexer_1 (
    .out0(demultiplexer_1_out0), .in(Load), .sel(Address[14]));  // open: out1
  Clock clock_1 (.out(clock_1_out));
  RAM #(.addrWidth(14), .dataWidth(16), .bus("separate")) ram_1 (
    .addr(Address[13:0]), .din(In), .data(Out), .str(demultiplexer_1_out0), .clk(clock_1_out), .ld(1'b1));  // open: sel, clr
endmodule
